# Fritzing sketch Aben_Motherboard (saved by Fritzing 0.9.3b)

parts:
  U1 = MAX485 [package=dil08]
  U2 = ESP32S-HiLetgo [part_number=ESP32S-HiLetgo]
  XLR1 = XLR3_NCFAH2 [package=xlr3_nc3fah2]
  V2 = DC Power [voltage=5V]

nets:
  N1: U1.DE, U1.VCC, U2.3.3
  N2: U1.DI, U2.GPIO18
  GND: U1.GND, U2.GND, V2.V-
  N3: U1.A, XLR1.3
  N4: U1.B, XLR1.2
  N5: U2.VIN, V2.V+

notes:
  DMX Output

custom parts:
  ESP32S-HiLetgo: HiLetgo ESP-WROOM-32 ESP32 ESP-32S Development Board 2.4GHz Dual-Mode WiFi + Bluetooth Dual Cores Microcontroller The ESP32 integrated with Antenna switches, RF Balun, power amplifiers, low-noise amplifiers, filters, and management modules, and the entire solution occupies the least area of PCB. 2.4 GHz Wi-Fi plus Bluetooth dual-mode chip, with TSMC Ultra-low power consumption 40nm technology,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
