# Fritzing sketch Aben_Portal (saved by Fritzing 0.9.3b)

parts:
  M1 = RioRand LM2596
  V1 = DC Power [voltage=24]
  HC-SR04_Sensor_1 = HC-SR04 Ultrasonic Distance Sensor
  XLR1 = XLR NC3MAAH [package=nc3maah]  # not connected
  U2 = NodeMCU V1.0

nets:
  N1: M1.Pin_1, V1.V+
  N2: M1.Pin_2, V1.V-
  VCC: M1.Pin_3, HC-SR04_Sensor_1.VCC, U2.Vin
  N3: M1.Pin_4, HC-SR04_Sensor_1.ECHO, U2.GND
  N4: HC-SR04_Sensor_1.TRIG, U2.D6
  N5: HC-SR04_Sensor_1.GND, U2.D7

notes:
  To DMX Controller and RGB Strip

custom parts:
  NodeMCU V1.0: ESP8266 based NodeMCU
